# Fritzing sketch victoria (saved by Fritzing 0.9.2b)
circuit board: 8.46667cm x 5.64444cm
breadboards: 1

parts:
  Part1 = Arduino Mega 2560 (Rev3)
  Q2 = Basic FET N-Channel [package="TO220 [THT]"]
  R1 = Resistor [tolerance=±5% resistance=100 package=THT]
  R2 = Resistor [tolerance=±5% resistance=10k package=THT]
  J1 = double row male pin header, 6 pins [form="♂ (male)"]
  JP1 = Header 2 [package=screwterminal-3.5mm-2_lock]
  Q3 = Basic FET N-Channel [package="TO220 [THT]"]
  R3 = Resistor [tolerance=±5% resistance=100 package=THT]
  R4 = Resistor [tolerance=±5% resistance=10k package=THT]
  J2 = double row male pin header, 8 pins [form="♂ (male)"]

nets:
  N1: Part1.D21/SCL, J1.pin6
  N2: Part1.D20/SDA, J1.pin5
  N3: Part1.D15/RX3, J1.pin2
  N4: Part1.D14/TX3, J1.pin3
  N5: Part1.GND, Q2.source, R2.Pin_1, JP1.2, Q3.source, R4.Pin_1
  N6: Part1.VIN, J1.pin1, JP1.1, J2.pin1
  N7: Part1.D24, R1.Pin_0
  N8: Part1.D27, R3.Pin_0
  N9: Part1.D48, J2.pin7
  N10: Part1.D49, J2.pin2
  N11: Part1.D50, J2.pin5
  N12: Part1.D51, J2.pin3
  N13: Part1.D52, J2.pin6
  N14: Q2.gate, R1.Pin_1, R2.Pin_0
  N15: Q2.drain, J1.pin4
  N16: Q3.gate, R3.Pin_1
  N17: Q3.drain, R4.Pin_0, J2.pin8
